# Fritzing sketch Paddle_of_Theseus (saved by Fritzing 0.9.3b)
breadboards: 1

parts:
  Part3 = Adafruit AT42QT1010 Standalone Momentary Capacitive Touch Sensor [part_number="Capacitive Touch"]
  Teensy_3_1 = Teensy 3.1
  6DOF = IMU Digital Combo Board 6DOF
  R5 = Resistor [tolerance=±5% resistance=1k package=THT]
  R6 = Resistor [tolerance=±5% resistance=10k package=THT]
  R7 = Resistor [tolerance=±5% resistance=10k package=THT]
  Ultrasonic_Sensor = PING Ultrasonic Sensor
  SparkFun1 = SoftPot Membrane Potentiometer - 50mm [part_number=SEN-08680]
  ENCODER1 = Rotary Encoder with Knob

nets:
  3V3: Part3.VDD, Teensy_3_1.3V3, 6DOF.3.3V, R7.Pin_0, Ultrasonic_Sensor.VCC, SparkFun1.leg1
  TEENSY_CAP_TOUCH_PIN: Part3.OUT, Teensy_3_1.D3
  GND: Part3.GND, Teensy_3_1.GND, 6DOF.GND, R5.Pin_1, R6.Pin_0, Ultrasonic_Sensor.GND, SparkFun1.leg2, ENCODER1.no_name_yet#5
  TEENSY_ULTRASONIC_PIN: Teensy_3_1.D0, Ultrasonic_Sensor.I/O
  TEENSY_ROT_ENC_BUTTON_PIN: Teensy_3_1.D1, ENCODER1.no_name_yet#4
  TEENSY_ROT_ENC_PIN: Teensy_3_1.D2, ENCODER1.no_name_yet#3
  TEENSY_LIN_POT_PIN: Teensy_3_1.A0/D14, R5.Pin_0, SparkFun1.wiper
  TEENSY_SDA_PIN: Teensy_3_1.A4/D18, 6DOF.SDA
  TEENSY_SCL_PIN: Teensy_3_1.A5/D19, 6DOF.SCL
  N1: R6.Pin_1, ENCODER1.no_name_yet#2
  N2: R7.Pin_1, ENCODER1.no_name_yet#1

custom parts:
  Adafruit AT42QT1010 Standalone Momentary Capacitive Touch Sensor: This breakout board is the simplest way to create a project with a single "momentary" capacitive touch sensor. No microcontroller is required here - just power with 1.8 to 5.5VDC and touch the pad to activate the sensor. When a capacitive load is detected (e.g. a person touches the sensor-pad area) the red LED lights up and the output pin goes high. You can also solder a wire to the middle pad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
  PING Ultrasonic Sensor: The PING)))™ ultrasonic sensor provides an easy method of distance measurement. This sensor is perfect for any number of applications that require you to perform measurements between moving or stationary objects. Interfacing to a microcontroller is a snap. A single I/O pin is used to trigger an ultrasonic burst (well above human hearing) and then "listen" for the echo return pulse. The sensor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
  SoftPot Membrane Potentiometer - 50mm: These are very thin variable potentiometers. By pressing down on various parts of the strip, the resistance linearly changes from 100Ohms to 10,000Ohms allowing the user to very accurately calculate the relative position on the strip. Can be used as an accurate positional indicator for CNC head positioning, variable user input (volume level input for example), straight user input (multiple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
  Rotary Encoder with Knob: Rotary Encoder with 1/4" Shaft and Knob
